// Logisim project Proj.circ as structural Verilog: 2 circuits, main circuit main
module main (
  output [3:0] Failed_Attempts
);

  wire _0, _1, _2, _3, _4, _5, _6, _7, _8, _9, C, pu_1_alarm, pu_1_correct_code, pu_1_locked;
  wire [3:0] pu_1_out_12, pu_1_out_13, pu_1_out_14, pu_1_out_16, pu_1_out_17, pu_1_out_18;

  LED Locked (.in(pu_1_locked));
  Hex_Digit_Display hex_digit_display_1 (.value(pu_1_out_12));  // open: dp
  Hex_Digit_Display hex_digit_display_2 (.value(pu_1_out_13));  // open: dp
  Hex_Digit_Display hex_digit_display_3 (.value(pu_1_out_14));  // open: dp
  Hex_Digit_Display hex_digit_display_4 (.value(pu_1_out_16));  // open: dp
  LED Alarm (.in(pu_1_alarm));
  Button u__1 (.out(_1));
  Button u__2 (.out(_2));
  Button u__3 (.out(_3));
  Button u__6 (.out(_6));
  Button u__4 (.out(_4));
  Button u__5 (.out(_5));
  Button u__9 (.out(_9));
  Button u__8 (.out(_8));
  Button u__7 (.out(_7));
  Button u__0 (.out(_0));
  Button u_C (.out(C));
  Hex_Digit_Display hex_digit_display_5 (.value(pu_1_out_17));  // open: dp
  Hex_Digit_Display hex_digit_display_6 (.value(pu_1_out_18));  // open: dp
  PU pu_1 (
    .Locked(pu_1_locked), .out_12(pu_1_out_12), .out_13(pu_1_out_13), .out_14(pu_1_out_14),
    .Alarm(pu_1_alarm), .out_16(pu_1_out_16), .out_17(pu_1_out_17), .out_18(pu_1_out_18), .in_1(_0),
    .in_2(_1), .in_3(_2), .in_4(_3), .in_5(_4), .in_6(_5), .in_7(_6), .in_8(_7), .in_9(_8), .in_10(_9),
    .in_11(C), .Correct_Code(pu_1_correct_code), .Failed_Attempts(Failed_Attempts));
  LED Correct (.in(pu_1_correct_code));
endmodule

module PU (
  input  in_1,
  input  in_2,
  input  in_3,
  input  in_4,
  input  in_5,
  input  in_6,
  input  in_7,
  input  in_8,
  input  in_9,
  input  in_10,
  input  in_11,
  output [3:0] out_12,
  output [3:0] out_13,
  output [3:0] out_14,
  output Alarm,
  output [3:0] out_16,
  output [3:0] out_17,
  output [3:0] out_18,
  output Locked,
  output Correct_Code,
  output [3:0] Failed_Attempts
);

  wire and_1_out, C, comparator_1_eq, comparator_2_eq, comparator_2_lt, comparator_3_eq, comparator_4_eq,
       counter_1_carry, d_ff_2_q, demultiplexer_1_out0, demultiplexer_1_out1, F, nor_1_out, nor_2_out,
       nor_3_out, nor_4_out, nor_5_out, nor_6_out, not_1_out, not_2_out, not_3_out, not_4_out, not_5_out,
       not_6_out, not_7_out, or_1_out, or_2_out, or_3_out, or_4_out, or_8_out, or_10_out, or_11_out,
       pull_resistor_1_node, pull_resistor_2_node, pull_resistor_3_node, pull_resistor_4_node;
  wire [3:0] counter_1_q, demultiplexer_2_out1, demultiplexer_2_out2, demultiplexer_2_out3,
       demultiplexer_2_out4, demultiplexer_2_out5, demultiplexer_2_out6, multiplexer_1_out, or_5_out,
       ram_1_data, ram_2_data, register_1_q, register_2_q;

  D_Flip_Flop d_ff_1 (.clk(and_1_out), .D(and_1_out), .Q(Locked), .reset(or_1_out));  // open: Qn, preset, en
  or or_1 (or_1_out, C, Correct_Code);
  and and_1 (and_1_out, d_ff_2_q, comparator_1_eq);
  Comparator #(.width(4)) comparator_1 (.a(4'b0000), .b(counter_1_q), .eq(comparator_1_eq));  // open: gt, lt
  Counter #(.width(4), .max('h7), .ongoal("load")) counter_1 (
    .Q(counter_1_q), .carry(counter_1_carry), .clk(or_3_out), .clr(C));  // open: load, D, count
  D_Flip_Flop d_ff_2 (.clk(counter_1_carry), .D(counter_1_carry), .Q(d_ff_2_q), .reset(C));  // open: Qn, preset, en
  Pull_Resistor pull_resistor_1 (.node(pull_resistor_1_node));
  Pull_Resistor pull_resistor_2 (.node(pull_resistor_2_node));
  Pull_Resistor pull_resistor_3 (.node(pull_resistor_3_node));
  Pull_Resistor pull_resistor_4 (.node(pull_resistor_4_node));
  Comparator #(.width(4)) comparator_2 (
    .a(4'b0110), .b(counter_1_q), .eq(comparator_2_eq), .lt(comparator_2_lt));  // open: gt
  or or_2 (or_2_out, comparator_2_eq, comparator_2_lt);
  not not_1 (not_1_out, or_2_out);
  or or_3 (or_3_out, in_1, pull_resistor_4_node, pull_resistor_3_node, pull_resistor_2_node, pull_resistor_1_node);
  assign pull_resistor_2_node = not_1_out ? or_5_out[2] : 1'bz;  // Controlled_Buffer controlled_buffer_1
  assign pull_resistor_4_node = not_1_out ? or_5_out[0] : 1'bz;  // Controlled_Buffer controlled_buffer_2
  assign pull_resistor_1_node = not_1_out ? or_5_out[3] : 1'bz;  // Controlled_Buffer controlled_buffer_3
  assign pull_resistor_3_node = not_1_out ? or_5_out[1] : 1'bz;  // Controlled_Buffer controlled_buffer_4
  or or_4 (or_4_out, F, C);
  not not_2 (not_2_out, or_3_out);
  Demultiplexer #(.enable("false")) demultiplexer_1 (
    .out0(demultiplexer_1_out0), .out1(demultiplexer_1_out1), .in(not_2_out), .sel(d_ff_2_q));
  Register #(.width(4), .trigger("high")) register_1 (.D(or_5_out), .Q(register_1_q), .clk(or_3_out));  // open: en, clr
  not not_3 (not_3_out, counter_1_q[2]);
  not not_4 (not_4_out, counter_1_q[1]);
  or or_5 (or_5_out[0], in_2, in_4, in_6, in_8, in_10);
  Comparator #(.width(4)) comparator_3 (.a(4'b0000), .b(counter_1_q), .eq(comparator_3_eq));  // open: gt, lt
  RAM #(.addrWidth(4), .dataWidth(4), .bus("separate")) ram_1 (
    .addr(counter_1_q), .din(register_1_q), .data(ram_1_data), .clk(demultiplexer_1_out1), .clr(or_4_out));  // open: str, sel, ld
  RAM #(.addrWidth(4), .dataWidth(4), .bus("separate")) ram_2 (
    .addr(counter_1_q), .din(register_1_q), .data(ram_2_data), .clk(demultiplexer_1_out0), .clr(C));  // open: str, sel, ld
  not not_5 (not_5_out, counter_1_q[2]);
  or or_6 (or_5_out[1], in_3, in_4, in_7, in_8);
  and and_2 (F, comparator_3_eq, Locked);
  Comparator #(.width(4)) comparator_4 (.a(ram_1_data), .b(ram_2_data), .eq(comparator_4_eq));  // open: gt, lt
  Demultiplexer #(.select(4), .width(4), .tristate("true"), .disabled(0), .enable("false")) demultiplexer_2 (
    .out1(demultiplexer_2_out1), .out2(demultiplexer_2_out2), .out3(demultiplexer_2_out3),
    .out4(demultiplexer_2_out4), .out5(demultiplexer_2_out5), .out6(demultiplexer_2_out6), .in(register_2_q),
    .sel(counter_1_q));  // open: out0, out7, out8, out9, out10, out11, out12, out13, out14, out15
  Register #(.width(4), .trigger("high")) register_2 (
    .D(multiplexer_1_out), .Q(register_2_q), .clk(not_2_out));  // open: en, clr
  Multiplexer #(.width(4), .enable("false")) multiplexer_1 (
    .in0(ram_2_data), .in1(ram_1_data), .out(multiplexer_1_out), .sel(d_ff_2_q));
  nor nor_1 (nor_1_out, counter_1_q[0], not_4_out, not_3_out, counter_1_q[3]);
  not not_6 (not_6_out, counter_1_q[0]);
  nor nor_2 (nor_2_out, counter_1_q[0], not_4_out, counter_1_q[2], counter_1_q[3]);
  nor nor_3 (nor_3_out, not_6_out, not_4_out, counter_1_q[2], counter_1_q[3]);
  or or_7 (or_5_out[2], in_5, in_6, in_7, in_8);
  not not_7 (not_7_out, Locked);
  Counter #(.width(4), .max('h6), .ongoal("stay")) counter_2 (
    .count(comparator_4_eq), .carry(Correct_Code), .clk(comparator_4_eq), .clr(or_8_out));  // open: load, D, Q
  or or_8 (or_8_out, counter_1_carry, C);
  nor nor_4 (nor_4_out, counter_1_q[1], not_6_out, counter_1_q[2], counter_1_q[3]);
  nor nor_5 (nor_5_out, counter_1_q[0], counter_1_q[1], not_5_out, counter_1_q[3]);
  nor nor_6 (nor_6_out, not_6_out, counter_1_q[1], not_5_out, counter_1_q[3]);
  or or_9 (or_5_out[3], in_9, in_10);
  Pull_Resistor pull_resistor_5 (.node(C));
  assign C = not_7_out ? in_11 : 1'bz;  // Controlled_Buffer controlled_buffer_5
  Counter #(.width(4), .max('h3), .ongoal("stay")) counter_3 (
    .count(Locked), .Q(Failed_Attempts), .carry(Alarm), .clk(comparator_3_eq), .clr(or_10_out));  // open: load, D
  or or_10 (or_10_out, Correct_Code, C);
  or or_11 (or_11_out, comparator_1_eq, C);
  Register #(.width(4), .trigger("high")) register_3 (
    .D(demultiplexer_2_out6), .en(1'b1), .Q(out_18), .clk(nor_1_out), .clr(or_11_out));
  Register #(.width(4), .trigger("high")) register_4 (
    .D(demultiplexer_2_out1), .en(1'b1), .Q(out_12), .clk(nor_4_out), .clr(or_11_out));
  Register #(.width(4), .trigger("high")) register_5 (
    .D(demultiplexer_2_out2), .en(1'b1), .Q(out_13), .clk(nor_2_out), .clr(or_11_out));
  Register #(.width(4), .trigger("high")) register_6 (
    .D(demultiplexer_2_out3), .en(1'b1), .Q(out_14), .clk(nor_3_out), .clr(or_11_out));
  Register #(.width(4), .trigger("high")) register_7 (
    .D(demultiplexer_2_out4), .en(1'b1), .Q(out_16), .clk(nor_5_out), .clr(or_11_out));
  Register #(.width(4), .trigger("high")) register_8 (
    .D(demultiplexer_2_out5), .en(1'b1), .Q(out_17), .clk(nor_6_out), .clr(or_11_out));

  // Other names for the same wires on the sheet: _0 = in_1; _1 = in_2; _2 = in_3; _3 = in_4; _4 = in_5; _5 = in_6;
  //   _6 = in_7; _7 = in_8; _8 = in_9; _9 = in_10; LCD1[3:0] = out_12; LCD2[3:0] = out_13; LCD3[3:0] = out_14;
  //   LCD4[3:0] = out_16; LCD5[3:0] = out_17; LCD6[3:0] = out_18
endmodule
